# Fritzing sketch led-sw (saved by Fritzing 0.9.10b)
breadboards: 1

parts:
  U1 = ESP32S-HiLetgo [part_number=ESP32S-HiLetgo]
  S1 = Pushbutton [package="[THT]"]
  S2 = Pushbutton [package="[THT]"]
  LED1 = LED - 3mm [color="Red (633nm)" current=0.030 package="3 mm [THT]"]
  LED2 = LED - 3mm [color="Red (633nm)" current=0.030 package="3 mm [THT]"]
  R1 = Resistor [tolerance=±5% power=0.25 resistance=220 package=THT]

nets:
  N1: U1.GPIO14, S2.Pin_1, S2.Pin_2
  N2: U1.GPIO12, S1.Pin_1, S1.Pin_2
  N3: U1.GND, S1.Pin_3, S1.Pin_4, S2.Pin_3, S2.Pin_4, R1.Pin_1
  N4: U1.GPIO22, LED2.anode
  N5: U1.GPIO23, LED1.anode
  N6: LED1.cathode, LED2.cathode, R1.Pin_0

custom parts:
  ESP32S-HiLetgo: HiLetgo ESP-WROOM-32 ESP32 ESP-32S Development Board 2.4GHz Dual-Mode WiFi + Bluetooth Dual Cores Microcontroller The ESP32 integrated with Antenna switches, RF Balun, power amplifiers, low-noise amplifiers, filters, and management modules, and the entire solution occupies the least area of PCB. 2.4 GHz Wi-Fi plus Bluetooth dual-mode chip, with TSMC Ultra-low power consumption 40nm technology,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
